// Logisim project MT16-Barrel-PC.circ as structural Verilog: 5 circuits, main circuit MT16_Computer
module ALU16 (
  input  [15:0] ACC,
  input  [15:0] MEM,
  input  [7:0] OPERAND,
  input  [3:0] OPCODE,
  output [15:0] RESULT
);

  wire [15:0] ADD_RESULT, AND_RESULT, IMM16, NOT_RESULT, OR_RESULT, SHL_RESULT, SHR_RESULT, SUB_RESULT,
       XOR_RESULT;

  assign IMM16 = {{8{1'b0}}, OPERAND};  // Bit_Extender bit_extender_1
  Adder #(.width(16)) adder_1 (.a(ACC), .b(MEM), .out(ADD_RESULT), .cin(1'b0));  // open: cout
  Subtractor #(.width(16)) subtractor_1 (.a(ACC), .b(MEM), .out(SUB_RESULT), .bin(1'b0));  // open: bout
  assign AND_RESULT = ACC & MEM;  // AND_Gate and_1, 16 bits wide
  assign OR_RESULT = ACC | MEM;  // OR_Gate or_1, 16 bits wide
  assign XOR_RESULT = ACC ^ MEM;  // XOR_Gate xor_1, 16 bits wide
  assign NOT_RESULT = ~ACC;  // NOT_Gate not_1, 16 bits wide
  Shifter #(.shift("ll"), .width(16)) shifter_1 (.in(ACC), .\dist (4'b0001), .out(SHL_RESULT));
  Shifter #(.shift("lr"), .width(16)) shifter_2 (.in(ACC), .\dist (4'b0001), .out(SHR_RESULT));
  Multiplexer #(.enable("false"), .select(4), .width(16)) multiplexer_1 (
    .in0(ACC), .in1(IMM16), .in2(MEM), .in3(ACC), .in4(ADD_RESULT), .in5(SUB_RESULT), .in6(AND_RESULT),
    .in7(OR_RESULT), .in8(XOR_RESULT), .in9(NOT_RESULT), .in10(SHL_RESULT), .in11(SHR_RESULT), .in12(ACC),
    .in13(ACC), .in14(MEM), .in15(ACC), .out(RESULT), .sel(OPCODE));

  // Other names for the same wires on the sheet: ACC_NEXT[15:0] = RESULT
endmodule

module MicrocodeControl (
  input  [3:0] Opcode,
  output [31:0] Control
);

  ROM #(.addrWidth(4), .dataWidth(32)) rom_1 (.addr(Opcode), .data(Control));

  // Notes on the sheet:
  //   contents of rom_1 (hex, n*v repeats v):
  //   00000000 00000081 00000082 00000100 0000008b 00000093 0000009b 000000a3 000000ab 000000b3 000000bb
  //   000000c3 00000200 00000600 0000098c 00001000
endmodule

module Scheduler4 (
  input  Clock,
  input  Reset,
  output [1:0] Thread
);

  wire [1:0] TID_NEXT;

  Adder #(.width(2)) adder_1 (.a(Thread), .b(2'b01), .out(TID_NEXT), .cin(1'b0));  // open: cout
  Register #(.trigger("rising"), .width(2)) RTID (.D(TID_NEXT), .en(1'b1), .Q(Thread), .clk(Clock), .clr(Reset));

  // Other names for the same wires on the sheet: TID[1:0] = Thread
endmodule

module MT16_Core (
  input  Clock,
  input  Reset,
  input  [7:0] PROG0,
  input  [7:0] PROG1,
  input  [7:0] PROG2,
  input  [7:0] PROG3,
  input  [15:0] MEM,
  output [15:0] OUT0,
  output [15:0] OUT1,
  output [15:0] OUT2,
  output [15:0] OUT3,
  output [15:0] ATOMIC_COUNT,
  output [1:0] TID,
  output [7:0] PC,
  output [15:0] ACC,
  output [7:0] IR,
  output [7:0] OPERAND,
  output [1:0] STATE,
  output CurrentHalt,
  output AllHalted,
  output [7:0] PC0,
  output [7:0] PC1,
  output [7:0] PC2,
  output [7:0] PC3,
  output [7:0] MEM_ADDRESS,
  output [15:0] MEM_WRITE_DATA,
  output MEM_WE
);

  wire ACC_WE, ACC_WE0, ACC_WE1, ACC_WE2, ACC_WE3, ACTIVE0, ACTIVE1, ACTIVE2, ACTIVE3, ADDR_ATOMIC_COUNT,
       ADDR_OUT0, ADDR_OUT1, ADDR_OUT2, ADDR_OUT3, BRANCH_OK, BRANCH_REQ, BRANCH_TAKEN, CTRL_ATOMIC,
       CTRL_COND, CTRL_HALT, CTRL_WACC, CTRL_WMEM, CTRL_WPC, EXECUTE, FETCH_ANY, FETCH_OPCODE, FETCH_OPERAND,
       HALT0, HALT1, HALT2, HALT3, HALT_WE, HALT_WE0, HALT_WE1, HALT_WE2, HALT_WE3, IR_WE0, IR_WE1, IR_WE2,
       IR_WE3, OPERAND_WE0, OPERAND_WE1, OPERAND_WE2, OPERAND_WE3, PC_WE, PC_WE0, PC_WE1, PC_WE2, PC_WE3,
       RUN, S0, S1, S2, STATE_WE0, STATE_WE1, STATE_WE2, STATE_WE3, UNCONDITIONAL, WE_ATOMIC_COUNT, WE_OUT0,
       WE_OUT1, WE_OUT2, WE_OUT3, ZERO, ZERO0, ZERO1, ZERO2, ZERO3, ZERO_NEXT, ZERO_WE0, ZERO_WE1, ZERO_WE2,
       ZERO_WE3;
  wire [1:0] STATE0, STATE1, STATE2, STATE3, STATE_NEXT, TID_NEXT;
  wire [2:0] CTRL_ACC_SOURCE;
  wire [3:0] CTRL_ALU_OP, OPCODE;
  wire [7:0] IR0, IR1, IR2, IR3, OPERAND0, OPERAND1, OPERAND2, OPERAND3, PC_NEXT, PC_PLUS1, PROG;
  wire [15:0] ACC0, ACC1, ACC2, ACC3, ACC_NEXT, ADD_RESULT, ALU_RESULT, AND_RESULT, IMM16, NOT_RESULT,
       OR_RESULT, SHL_RESULT, SHR_RESULT, SUB_RESULT, XOR_RESULT;
  wire [31:0] CONTROL, CONTROL_SHIFT3;

  and and_1 (PC_WE0, PC_WE, ACTIVE0);
  and and_2 (PC_WE1, PC_WE, ACTIVE1);
  and and_3 (PC_WE2, PC_WE, ACTIVE2);
  and and_4 (PC_WE3, PC_WE, ACTIVE3);
  Adder #(.width(2)) adder_1 (.a(TID), .b(2'b01), .out(TID_NEXT), .cin(1'b0));  // open: cout
  Register #(.trigger("rising")) RPC0 (.D(PC_NEXT), .en(PC_WE0), .Q(PC0), .clk(Clock), .clr(Reset));
  Register #(.trigger("rising")) RPC1 (.D(PC_NEXT), .en(PC_WE1), .Q(PC1), .clk(Clock), .clr(Reset));
  Register #(.trigger("rising")) RPC2 (.D(PC_NEXT), .en(PC_WE2), .Q(PC2), .clk(Clock), .clr(Reset));
  Register #(.trigger("rising")) RPC3 (.D(PC_NEXT), .en(PC_WE3), .Q(PC3), .clk(Clock), .clr(Reset));
  Multiplexer #(.enable("false"), .select(2), .width(8)) multiplexer_1 (
    .in0(PC0), .in1(PC1), .in2(PC2), .in3(PC3), .out(PC), .sel(TID));
  Register #(.trigger("rising"), .width(2)) RTID (.D(TID_NEXT), .en(1'b1), .Q(TID), .clk(Clock), .clr(Reset));
  and and_5 (ACC_WE0, ACC_WE, ACTIVE0);
  and and_6 (ACC_WE1, ACC_WE, ACTIVE1);
  and and_7 (ACC_WE2, ACC_WE, ACTIVE2);
  and and_8 (ACC_WE3, ACC_WE, ACTIVE3);
  assign IMM16 = {{8{1'b0}}, MEM_ADDRESS};  // Bit_Extender bit_extender_1
  Multiplexer #(.enable("false"), .select(2), .width(8)) multiplexer_2 (
    .in0(PROG0), .in1(PROG1), .in2(PROG2), .in3(PROG3), .out(PROG), .sel(TID));
  Adder #(.width(16)) adder_2 (.a(ACC), .b(MEM), .out(ADD_RESULT), .cin(1'b0));  // open: cout
  Subtractor #(.width(16)) subtractor_1 (.a(ACC), .b(MEM), .out(SUB_RESULT), .bin(1'b0));  // open: bout
  assign AND_RESULT = ACC & MEM;  // AND_Gate and_9, 16 bits wide
  assign OR_RESULT = ACC | MEM;  // OR_Gate or_1, 16 bits wide
  assign XOR_RESULT = ACC ^ MEM;  // XOR_Gate xor_1, 16 bits wide
  assign NOT_RESULT = ~ACC;  // NOT_Gate not_1, 16 bits wide
  Shifter #(.shift("ll"), .width(16)) shifter_1 (.in(ACC), .\dist (4'b0001), .out(SHL_RESULT));
  Shifter #(.shift("lr"), .width(16)) shifter_2 (.in(ACC), .\dist (4'b0001), .out(SHR_RESULT));
  Decoder #(.enable("false"), .select(2)) decoder_1 (
    .out0(ACTIVE0), .out1(ACTIVE1), .out2(ACTIVE2), .out3(ACTIVE3), .sel(TID));
  Register #(.trigger("rising"), .width(16)) RACC0 (.D(ACC_NEXT), .en(ACC_WE0), .Q(ACC0), .clk(Clock), .clr(Reset));
  Register #(.trigger("rising"), .width(16)) RACC1 (.D(ACC_NEXT), .en(ACC_WE1), .Q(ACC1), .clk(Clock), .clr(Reset));
  Register #(.trigger("rising"), .width(16)) RACC2 (.D(ACC_NEXT), .en(ACC_WE2), .Q(ACC2), .clk(Clock), .clr(Reset));
  Register #(.trigger("rising"), .width(16)) RACC3 (.D(ACC_NEXT), .en(ACC_WE3), .Q(ACC3), .clk(Clock), .clr(Reset));
  and and_10 (IR_WE0, FETCH_OPCODE, ACTIVE0);
  and and_11 (IR_WE1, FETCH_OPCODE, ACTIVE1);
  and and_12 (IR_WE2, FETCH_OPCODE, ACTIVE2);
  and and_13 (IR_WE3, FETCH_OPCODE, ACTIVE3);
  Multiplexer #(.enable("false"), .select(2), .width(16)) multiplexer_3 (
    .in0(ACC0), .in1(ACC1), .in2(ACC2), .in3(ACC3), .out(ACC), .sel(TID));
  Register #(.trigger("rising")) RIR0 (.D(PROG), .en(IR_WE0), .Q(IR0), .clk(Clock), .clr(Reset));
  Register #(.trigger("rising")) RIR1 (.D(PROG), .en(IR_WE1), .Q(IR1), .clk(Clock), .clr(Reset));
  Register #(.trigger("rising")) RIR2 (.D(PROG), .en(IR_WE2), .Q(IR2), .clk(Clock), .clr(Reset));
  Register #(.trigger("rising")) RIR3 (.D(PROG), .en(IR_WE3), .Q(IR3), .clk(Clock), .clr(Reset));
  Multiplexer #(.enable("false"), .select(4), .width(16)) multiplexer_4 (
    .in0(ACC), .in1(ADD_RESULT), .in2(SUB_RESULT), .in3(AND_RESULT), .in4(OR_RESULT), .in5(XOR_RESULT),
    .in6(NOT_RESULT), .in7(SHL_RESULT), .in8(SHR_RESULT), .in9(ACC), .in10(ACC), .in11(ACC), .in12(ACC),
    .in13(ACC), .in14(ACC), .in15(ACC), .out(ALU_RESULT), .sel(CTRL_ALU_OP));
  Multiplexer #(.enable("false"), .select(2), .width(8)) multiplexer_5 (
    .in0(IR0), .in1(IR1), .in2(IR2), .in3(IR3), .out(IR), .sel(TID));
  BitSelector #(.group(4), .width(8)) bitselector_1 (.in(IR), .out(OPCODE), .sel(1'b0));
  and and_14 (OPERAND_WE0, FETCH_OPERAND, ACTIVE0);
  and and_15 (OPERAND_WE1, FETCH_OPERAND, ACTIVE1);
  and and_16 (OPERAND_WE2, FETCH_OPERAND, ACTIVE2);
  and and_17 (OPERAND_WE3, FETCH_OPERAND, ACTIVE3);
  ROM #(.addrWidth(4), .dataWidth(32)) CONTROL_ROM (.addr(OPCODE), .data(CONTROL));
  Register #(.trigger("rising")) ROPERAND0 (.D(PROG), .en(OPERAND_WE0), .Q(OPERAND0), .clk(Clock), .clr(Reset));
  Register #(.trigger("rising")) ROPERAND1 (.D(PROG), .en(OPERAND_WE1), .Q(OPERAND1), .clk(Clock), .clr(Reset));
  Register #(.trigger("rising")) ROPERAND2 (.D(PROG), .en(OPERAND_WE2), .Q(OPERAND2), .clk(Clock), .clr(Reset));
  Register #(.trigger("rising")) ROPERAND3 (.D(PROG), .en(OPERAND_WE3), .Q(OPERAND3), .clk(Clock), .clr(Reset));
  Multiplexer #(.enable("false"), .select(3), .width(16)) multiplexer_6 (
    .in0(ACC), .in1(IMM16), .in2(MEM), .in3(ALU_RESULT), .in4(MEM), .in5(ACC), .in6(ACC), .in7(ACC),
    .out(ACC_NEXT), .sel(CTRL_ACC_SOURCE));
  and and_18 (ACC_WE, EXECUTE, CTRL_WACC);
  Comparator #(.mode("unsigned"), .width(16)) comparator_1 (
    .a(ACC_NEXT), .b({16{1'b0}}), .eq(ZERO_NEXT));  // open: gt, lt
  and and_19 (STATE_WE0, RUN, ACTIVE0);
  and and_20 (STATE_WE1, RUN, ACTIVE1);
  and and_21 (STATE_WE2, RUN, ACTIVE2);
  and and_22 (STATE_WE3, RUN, ACTIVE3);
  Multiplexer #(.enable("false"), .select(2), .width(8)) multiplexer_7 (
    .in0(OPERAND0), .in1(OPERAND1), .in2(OPERAND2), .in3(OPERAND3), .out(MEM_ADDRESS), .sel(TID));
  Register #(.trigger("rising"), .width(2)) RSTATE0 (
    .D(STATE_NEXT), .en(STATE_WE0), .Q(STATE0), .clk(Clock), .clr(Reset));
  Register #(.trigger("rising"), .width(2)) RSTATE1 (
    .D(STATE_NEXT), .en(STATE_WE1), .Q(STATE1), .clk(Clock), .clr(Reset));
  Register #(.trigger("rising"), .width(2)) RSTATE2 (
    .D(STATE_NEXT), .en(STATE_WE2), .Q(STATE2), .clk(Clock), .clr(Reset));
  Register #(.trigger("rising"), .width(2)) RSTATE3 (
    .D(STATE_NEXT), .en(STATE_WE3), .Q(STATE3), .clk(Clock), .clr(Reset));
  BitSelector #(.group(3), .width(32)) bitselector_2 (.in(CONTROL), .out(CTRL_ACC_SOURCE), .sel(4'b0000));
  Shifter #(.shift("lr"), .width(32)) shifter_3 (.in(CONTROL), .\dist (5'b00011), .out(CONTROL_SHIFT3));
  Multiplexer #(.enable("false"), .select(2), .width(2)) multiplexer_8 (
    .in0(STATE0), .in1(STATE1), .in2(STATE2), .in3(STATE3), .out(STATE), .sel(TID));
  BitSelector #(.group(4), .width(32)) bitselector_3 (.in(CONTROL_SHIFT3), .out(CTRL_ALU_OP), .sel(3'b000));
  BitSelector #(.group(1), .width(32)) bitselector_4 (.in(CONTROL), .out(CTRL_WACC), .sel(5'b00111));
  Comparator #(.mode("unsigned"), .width(2)) comparator_2 (.a(STATE), .b(2'b00), .eq(S0));  // open: gt, lt
  Comparator #(.mode("unsigned"), .width(2)) comparator_3 (.a(STATE), .b(2'b01), .eq(S1));  // open: gt, lt
  Comparator #(.mode("unsigned"), .width(2)) comparator_4 (.a(STATE), .b(2'b10), .eq(S2));  // open: gt, lt
  Adder #(.width(8)) adder_3 (.a(PC), .b(8'h1), .out(PC_PLUS1), .cin(1'b0));  // open: cout
  Multiplexer #(.enable("false"), .select(1), .width(16)) multiplexer_9 (
    .in0(ACC), .in1(ADD_RESULT), .out(MEM_WRITE_DATA), .sel(CTRL_ATOMIC));
  and and_23 (ZERO_WE0, ACC_WE, ACTIVE0);
  and and_24 (ZERO_WE1, ACC_WE, ACTIVE1);
  and and_25 (ZERO_WE2, ACC_WE, ACTIVE2);
  and and_26 (ZERO_WE3, ACC_WE, ACTIVE3);
  BitSelector #(.group(1), .width(32)) bitselector_5 (.in(CONTROL), .out(CTRL_WMEM), .sel(5'b01000));
  Register #(.trigger("rising"), .width(1)) RZERO0 (.D(ZERO_NEXT), .en(ZERO_WE0), .Q(ZERO0), .clk(Clock), .clr(Reset));
  Register #(.trigger("rising"), .width(1)) RZERO1 (.D(ZERO_NEXT), .en(ZERO_WE1), .Q(ZERO1), .clk(Clock), .clr(Reset));
  Register #(.trigger("rising"), .width(1)) RZERO2 (.D(ZERO_NEXT), .en(ZERO_WE2), .Q(ZERO2), .clk(Clock), .clr(Reset));
  Register #(.trigger("rising"), .width(1)) RZERO3 (.D(ZERO_NEXT), .en(ZERO_WE3), .Q(ZERO3), .clk(Clock), .clr(Reset));
  BitSelector #(.group(1), .width(32)) bitselector_6 (.in(CONTROL), .out(CTRL_WPC), .sel(5'b01001));
  BitSelector #(.group(1), .width(32)) bitselector_7 (.in(CONTROL), .out(CTRL_COND), .sel(5'b01010));
  not not_2 (RUN, CurrentHalt);
  not not_3 (UNCONDITIONAL, CTRL_COND);
  and and_27 (MEM_WE, EXECUTE, CTRL_WMEM);
  and and_28 (HALT_WE0, HALT_WE, ACTIVE0);
  and and_29 (HALT_WE1, HALT_WE, ACTIVE1);
  and and_30 (HALT_WE2, HALT_WE, ACTIVE2);
  and and_31 (HALT_WE3, HALT_WE, ACTIVE3);
  Multiplexer #(.enable("false"), .select(2)) multiplexer_10 (
    .in0(ZERO0), .in1(ZERO1), .in2(ZERO2), .in3(ZERO3), .out(ZERO), .sel(TID));
  BitSelector #(.group(1), .width(32)) bitselector_8 (.in(CONTROL), .out(CTRL_ATOMIC), .sel(5'b01011));
  and and_32 (FETCH_OPCODE, RUN, S0);
  and and_33 (FETCH_OPERAND, RUN, S1);
  and and_34 (EXECUTE, RUN, S2);
  or or_2 (BRANCH_OK, UNCONDITIONAL, ZERO);
  and and_35 (HALT_WE, EXECUTE, CTRL_HALT);
  Register #(.trigger("rising"), .width(1)) RHALT0 (.D(1'b1), .en(HALT_WE0), .Q(HALT0), .clk(Clock), .clr(Reset));
  Register #(.trigger("rising"), .width(1)) RHALT1 (.D(1'b1), .en(HALT_WE1), .Q(HALT1), .clk(Clock), .clr(Reset));
  Register #(.trigger("rising"), .width(1)) RHALT2 (.D(1'b1), .en(HALT_WE2), .Q(HALT2), .clk(Clock), .clr(Reset));
  Register #(.trigger("rising"), .width(1)) RHALT3 (.D(1'b1), .en(HALT_WE3), .Q(HALT3), .clk(Clock), .clr(Reset));
  BitSelector #(.group(1), .width(32)) bitselector_9 (.in(CONTROL), .out(CTRL_HALT), .sel(5'b01100));
  and and_36 (BRANCH_REQ, EXECUTE, CTRL_WPC);
  or or_3 (FETCH_ANY, FETCH_OPCODE, FETCH_OPERAND);
  Multiplexer #(.enable("false"), .select(2)) multiplexer_11 (
    .in0(HALT0), .in1(HALT1), .in2(HALT2), .in3(HALT3), .out(CurrentHalt), .sel(TID));
  Multiplexer #(.enable("false"), .select(2), .width(2)) multiplexer_12 (
    .in0(2'b01), .in1(2'b10), .in2(2'b00), .in3(2'b00), .out(STATE_NEXT), .sel(STATE));
  and and_37 (BRANCH_TAKEN, BRANCH_REQ, BRANCH_OK);
  or or_4 (PC_WE, FETCH_ANY, BRANCH_TAKEN);
  Multiplexer #(.enable("false"), .select(1), .width(8)) multiplexer_13 (
    .in0(PC_PLUS1), .in1(MEM_ADDRESS), .out(PC_NEXT), .sel(BRANCH_TAKEN));
  Comparator #(.mode("unsigned")) comparator_5 (.a(MEM_ADDRESS), .b(8'hf0), .eq(ADDR_OUT0));  // open: gt, lt
  Comparator #(.mode("unsigned")) comparator_6 (.a(MEM_ADDRESS), .b(8'hf1), .eq(ADDR_OUT1));  // open: gt, lt
  Comparator #(.mode("unsigned")) comparator_7 (.a(MEM_ADDRESS), .b(8'hf2), .eq(ADDR_OUT2));  // open: gt, lt
  Comparator #(.mode("unsigned")) comparator_8 (.a(MEM_ADDRESS), .b(8'hf3), .eq(ADDR_OUT3));  // open: gt, lt
  Comparator #(.mode("unsigned")) comparator_9 (.a(MEM_ADDRESS), .b(8'h30), .eq(ADDR_ATOMIC_COUNT));  // open: gt, lt
  and and_38 (WE_OUT0, MEM_WE, ADDR_OUT0);
  and and_39 (WE_OUT1, MEM_WE, ADDR_OUT1);
  and and_40 (WE_OUT2, MEM_WE, ADDR_OUT2);
  and and_41 (WE_OUT3, MEM_WE, ADDR_OUT3);
  and and_42 (WE_ATOMIC_COUNT, MEM_WE, ADDR_ATOMIC_COUNT);
  Register #(.trigger("rising"), .width(16)) ROUT0 (
    .D(MEM_WRITE_DATA), .en(WE_OUT0), .Q(OUT0), .clk(Clock), .clr(Reset));
  Register #(.trigger("rising"), .width(16)) ROUT1 (
    .D(MEM_WRITE_DATA), .en(WE_OUT1), .Q(OUT1), .clk(Clock), .clr(Reset));
  Register #(.trigger("rising"), .width(16)) ROUT2 (
    .D(MEM_WRITE_DATA), .en(WE_OUT2), .Q(OUT2), .clk(Clock), .clr(Reset));
  Register #(.trigger("rising"), .width(16)) ROUT3 (
    .D(MEM_WRITE_DATA), .en(WE_OUT3), .Q(OUT3), .clk(Clock), .clr(Reset));
  Register #(.trigger("rising"), .width(16)) RATOMIC_COUNT (
    .D(MEM_WRITE_DATA), .en(WE_ATOMIC_COUNT), .Q(ATOMIC_COUNT), .clk(Clock), .clr(Reset));
  and and_43 (AllHalted, HALT0, HALT1, HALT2, HALT3);

  assign OPERAND = MEM_ADDRESS;

  // Other names for the same wires on the sheet: ALL_HALTED = AllHalted; HALT = CurrentHalt; IR_WE = FETCH_OPCODE;
  //   OPERAND_WE = FETCH_OPERAND; STATE_WE = RUN; ZERO_WE = ACC_WE

  // Notes on the sheet:
  //   contents of CONTROL_ROM (hex, n*v repeats v):
  //   00000000 00000081 00000082 00000100 0000008b 00000093 0000009b 000000a3 000000ab 000000b3 000000bb
  //   000000c3 00000200 00000600 0000098c 00001000
endmodule

module MT16_Computer (
  input  Clock,
  input  Reset,
  output [15:0] OUT0,
  output [15:0] OUT1,
  output [15:0] OUT2,
  output [15:0] OUT3,
  output [15:0] ATOMIC_COUNT,
  output AllHalted,
  output [1:0] TID,
  output [7:0] PC,
  output [15:0] ACC,
  output [7:0] IR,
  output [7:0] OPERAND,
  output [1:0] STATE,
  output CurrentHalt
);

  wire button_1_out, clock_1_out, mt16_core_1_mem_we, or_1_out, or_2_out;
  wire [7:0] mt16_core_1_mem_address, mt16_core_1_pc0, mt16_core_1_pc1, mt16_core_1_pc2, mt16_core_1_pc3,
       THREAD_0_PROGRAM_data, THREAD_1_PROGRAM_data, THREAD_2_PROGRAM_data, THREAD_3_PROGRAM_data;
  wire [15:0] mt16_core_1_mem_write_data, SHARED_RAM_dout;

  Clock clock_1 (.out(clock_1_out));
  Button button_1 (.out(button_1_out));
  or or_1 (or_1_out, clock_1_out, Clock);
  or or_2 (or_2_out, button_1_out, Reset);
  ROM #(.addrWidth(8), .dataWidth(8)) THREAD_0_PROGRAM (.addr(mt16_core_1_pc0), .data(THREAD_0_PROGRAM_data));
  ROM #(.addrWidth(8), .dataWidth(8)) THREAD_1_PROGRAM (.addr(mt16_core_1_pc1), .data(THREAD_1_PROGRAM_data));
  ROM #(.addrWidth(8), .dataWidth(8)) THREAD_2_PROGRAM (.addr(mt16_core_1_pc2), .data(THREAD_2_PROGRAM_data));
  ROM #(.addrWidth(8), .dataWidth(8)) THREAD_3_PROGRAM (.addr(mt16_core_1_pc3), .data(THREAD_3_PROGRAM_data));
  MT16_Core mt16_core_1 (
    .Clock(or_1_out), .Reset(or_2_out), .PC0(mt16_core_1_pc0), .PROG0(THREAD_0_PROGRAM_data),
    .PC1(mt16_core_1_pc1), .PROG1(THREAD_1_PROGRAM_data), .PC2(mt16_core_1_pc2),
    .PROG2(THREAD_2_PROGRAM_data), .PC3(mt16_core_1_pc3), .PROG3(THREAD_3_PROGRAM_data), .OUT0(OUT0),
    .OUT1(OUT1), .OUT2(OUT2), .OUT3(OUT3), .ATOMIC_COUNT(ATOMIC_COUNT), .AllHalted(AllHalted),
    .MEM_ADDRESS(mt16_core_1_mem_address), .MEM_WE(mt16_core_1_mem_we),
    .MEM_WRITE_DATA(mt16_core_1_mem_write_data), .MEM(SHARED_RAM_dout), .TID(TID), .PC(PC), .ACC(ACC),
    .IR(IR), .OPERAND(OPERAND), .STATE(STATE), .CurrentHalt(CurrentHalt));
  RAM #(.addrWidth(8), .asyncread("true"), .byteenables("NobyteEnables"), .dataWidth(16), .databus("bibus"), .enables("byte"), .trigger("rising"), .clearpin("true")) SHARED_RAM (
    .addr(mt16_core_1_mem_address), .we(mt16_core_1_mem_we), .oe(1'b1), .clk(or_1_out),
    .din(mt16_core_1_mem_write_data), .dout(SHARED_RAM_dout));  // open: clr
  // LED #(.offColor("#37474f"), .onColor("#00c853")) led_1: pin names not known

  // Notes on the sheet:
  //   MT16 · 4-ПОТОЧНЫЙ МИКРОПРОГРАММНЫЙ КОМПЬЮТЕР
  //   Программа уже в ROM: нажмите ▶ Ticks Enabled — вычисления начнутся сразу
  //   УПРАВЛЕНИЕ
  //   автотакт
  //   сброс
  //   ПРОГРАММЫ ПОТОКОВ · 4 × ROM 256 × 8
  //   SUM 1…10 → OUT0
  //   contents of THREAD_0_PROGRAM (hex, n*v repeats v):
  //   01 01 03 01 01 0b 03 0b 01 00 03 10 01 01 03 11 02 10 04 11 03 10 02 11 04 01 03 11 05 0b 0d 22 0c
  //   10 02 10 03 f0 01 01 0e 30 0f 00 00 00 00 00 00 00 00 00 00 00 00 00 00 00 00 00 00 00 00 00 00 00
  //   00 00 00 00 00 00 00 00 00 00 00 00 00 00 00 00 00 00 00 00 00 00 00 00 00 00 00 00 00 00 00 00 00
  //   00 00 00 00 00 00 00 00 00 00 00 00 00 00 00 00 00 00 00 00 00 00 00 00 00 00 00 00 00 00 00 00 00
  //   00 00 00 00 00 00 00 00 00 00 00 00 00 00 00 00 00 00 00 00 00 00 00 00 00 00 00 00 00 00 00 00 00
  //   00 00 00 00 00 00 00 00 00 00 00 00 00 00 00 00 00 00 00 00 00 00 00 00 00 00 00 00 00 00 00 00 00
  //   00 00 00 00 00 00 00 00 00 00 00 00 00 00 00 00 00 00 00 00 00 00 00 00 00 00 00 00 00 00 00 00 00
  //   00 00 00 00 00 00 00 00 00 00 00 00 00 00 00 00 00 00 00 00 00 00 00 00 00
  //   T0
  //   AND · OR · XOR · NOT → OUT1
  //   contents of THREAD_1_PROGRAM (hex, n*v repeats v):
  //   01 ff 03 02 01 aa 03 20 01 0f 07 20 08 20 09 00 06 02 03 f1 01 01 0e 30 0f 00 00 00 00 00 00 00 00
  //   00 00 00 00 00 00 00 00 00 00 00 00 00 00 00 00 00 00 00 00 00 00 00 00 00 00 00 00 00 00 00 00 00
  //   00 00 00 00 00 00 00 00 00 00 00 00 00 00 00 00 00 00 00 00 00 00 00 00 00 00 00 00 00 00 00 00 00
  //   00 00 00 00 00 00 00 00 00 00 00 00 00 00 00 00 00 00 00 00 00 00 00 00 00 00 00 00 00 00 00 00 00
  //   00 00 00 00 00 00 00 00 00 00 00 00 00 00 00 00 00 00 00 00 00 00 00 00 00 00 00 00 00 00 00 00 00
  //   00 00 00 00 00 00 00 00 00 00 00 00 00 00 00 00 00 00 00 00 00 00 00 00 00 00 00 00 00 00 00 00 00
  //   00 00 00 00 00 00 00 00 00 00 00 00 00 00 00 00 00 00 00 00 00 00 00 00 00 00 00 00 00 00 00 00 00
  //   00 00 00 00 00 00 00 00 00 00 00 00 00 00 00 00 00 00 00 00 00 00 00 00 00
  //   T1
  //   SHL · SHR → OUT2
  //   contents of THREAD_2_PROGRAM (hex, n*v repeats v):
  //   01 03 0a 00 0a 00 0a 00 0a 00 0b 00 03 f2 01 01 0e 30 0f 00 00 00 00 00 00 00 00 00 00 00 00 00 00
  //   00 00 00 00 00 00 00 00 00 00 00 00 00 00 00 00 00 00 00 00 00 00 00 00 00 00 00 00 00 00 00 00 00
  //   00 00 00 00 00 00 00 00 00 00 00 00 00 00 00 00 00 00 00 00 00 00 00 00 00 00 00 00 00 00 00 00 00
  //   00 00 00 00 00 00 00 00 00 00 00 00 00 00 00 00 00 00 00 00 00 00 00 00 00 00 00 00 00 00 00 00 00
  //   00 00 00 00 00 00 00 00 00 00 00 00 00 00 00 00 00 00 00 00 00 00 00 00 00 00 00 00 00 00 00 00 00
  //   00 00 00 00 00 00 00 00 00 00 00 00 00 00 00 00 00 00 00 00 00 00 00 00 00 00 00 00 00 00 00 00 00
  //   00 00 00 00 00 00 00 00 00 00 00 00 00 00 00 00 00 00 00 00 00 00 00 00 00 00 00 00 00 00 00 00 00
  //   00 00 00 00 00 00 00 00 00 00 00 00 00 00 00 00 00 00 00 00 00 00 00 00 00
  //   T2
  //   40 + 2 → OUT3
  //   contents of THREAD_3_PROGRAM (hex, n*v repeats v):
  //   01 28 03 21 01 02 04 21 03 f3 01 01 0e 30 0f 00 00 00 00 00 00 00 00 00 00 00 00 00 00 00 00 00 00
  //   00 00 00 00 00 00 00 00 00 00 00 00 00 00 00 00 00 00 00 00 00 00 00 00 00 00 00 00 00 00 00 00 00
  //   00 00 00 00 00 00 00 00 00 00 00 00 00 00 00 00 00 00 00 00 00 00 00 00 00 00 00 00 00 00 00 00 00
  //   00 00 00 00 00 00 00 00 00 00 00 00 00 00 00 00 00 00 00 00 00 00 00 00 00 00 00 00 00 00 00 00 00
  //   00 00 00 00 00 00 00 00 00 00 00 00 00 00 00 00 00 00 00 00 00 00 00 00 00 00 00 00 00 00 00 00 00
  //   00 00 00 00 00 00 00 00 00 00 00 00 00 00 00 00 00 00 00 00 00 00 00 00 00 00 00 00 00 00 00 00 00
  //   00 00 00 00 00 00 00 00 00 00 00 00 00 00 00 00 00 00 00 00 00 00 00 00 00 00 00 00 00 00 00 00 00
  //   00 00 00 00 00 00 00 00 00 00 00 00 00 00 00 00 00 00 00 00 00 00 00 00 00
  //   T3
  //   FETCH OPCODE  →  FETCH OPERAND  →  EXECUTE  →  следующий поток
  //   ТЕКУЩИЙ КОНТЕКСТ / ОТЛАДКА
  //   РЕЗУЛЬТАТЫ ВСТРОЕННОЙ ПРОГРАММЫ
  //   OUT0 · сумма 1…10
  //   OUT1 · логика
  //   OUT2 · сдвиги
  //   OUT3 · арифметика
  //   ATOMIC · 4 потока
  //   ОБЩАЯ ПАМЯТЬ ДАННЫХ 256 × 16
  //   ГОТОВО / ALL HALTED
endmodule
