// Logisim project ЭВМ-7400.circ as structural Verilog: 23 circuits, main circuit ЭВМ_7400
module D_Flip_Flop (
  input  SET,
  input  D,
  input  CLK,
  input  CLR,
  output Q,
  output R
);

  D_Flip_Flop_part d_ff_1 (.clk(CLK), .D(D), .Q(Q), .Qn(R), .preset(SET), .reset(CLR));
endmodule

// 7404
module DIP_7404 (
  input  A1,
  input  A2,
  input  A3,
  input  A4,
  input  A5,
  input  A6,
  output Y1,
  output Y2,
  output Y3,
  output Y4,
  output Y5,
  output Y6
);

  not not_1 (Y1, A1);
  not not_2 (Y2, A2);
  not not_3 (Y3, A3);
  not not_4 (Y4, A4);
  not not_5 (Y5, A5);
  not not_6 (Y6, A6);
endmodule

// 7408
module DIP_7408 (
  input  A1,
  input  B1,
  input  A2,
  input  B2,
  input  A3,
  input  B3,
  input  A4,
  input  B4,
  output Y1,
  output Y2,
  output Y3,
  output Y4
);

  and and_1 (Y1, A1, B1);
  and and_2 (Y2, A2, B2);
  and and_3 (Y3, A3, B3);
  and and_4 (Y4, A4, B4);
endmodule

// 7430
module DIP_7430 (
  input  A,
  input  B,
  input  C,
  input  D,
  input  E,
  input  F,
  input  G,
  input  H,
  output Y
);

  nand nand_1 (Y, A, B, C, D, E, F, G, H);
endmodule

// 7432
module DIP_7432 (
  input  A1,
  input  B1,
  input  A2,
  input  B2,
  input  A3,
  input  B3,
  input  A4,
  input  B4,
  output Y1,
  output Y2,
  output Y3,
  output Y4
);

  or or_1 (Y1, A1, B1);
  or or_2 (Y2, A2, B2);
  or or_3 (Y3, A3, B3);
  or or_4 (Y4, A4, B4);
endmodule

// 7486
module DIP_7486 (
  input  A1,
  input  B1,
  input  A2,
  input  B2,
  input  A3,
  input  B3,
  input  A4,
  input  B4,
  output Y1,
  output Y2,
  output Y3,
  output Y4
);

  xor xor_1 (Y1, A1, B1);
  xor xor_2 (Y2, A2, B2);
  xor xor_3 (Y3, A3, B3);
  xor xor_4 (Y4, A4, B4);
endmodule

// 74157
module DIP_74157 (
  input  A1,
  input  B1,
  input  A2,
  input  B2,
  input  A3,
  input  B3,
  input  A4,
  input  B4,
  input  S0,
  input  OE,
  output Y1,
  output Y2,
  output Y3,
  output Y4
);

  wire and_1_out, and_2_out, and_3_out, and_4_out, and_5_out, and_6_out, and_7_out, and_8_out, not_1_out,
       not_2_out;

  not not_1 (not_1_out, S0);
  not not_2 (not_2_out, OE);
  and and_1 (and_1_out, A1, not_1_out, not_2_out);
  and and_2 (and_2_out, B1, S0, not_2_out);
  and and_3 (and_3_out, A2, not_1_out, not_2_out);
  and and_4 (and_4_out, B2, S0, not_2_out);
  and and_5 (and_5_out, A3, not_1_out, not_2_out);
  and and_6 (and_6_out, B3, S0, not_2_out);
  and and_7 (and_7_out, A4, not_1_out, not_2_out);
  and and_8 (and_8_out, B4, S0, not_2_out);
  or or_1 (Y1, and_1_out, and_2_out);
  or or_2 (Y2, and_3_out, and_4_out);
  or or_3 (Y3, and_5_out, and_6_out);
  or or_4 (Y4, and_7_out, and_8_out);
endmodule

// 74244
module DIP_74244 (
  input  A1,
  input  A2,
  input  A3,
  input  A4,
  input  OEA,
  input  B1,
  input  B2,
  input  B3,
  input  B4,
  input  OEB,
  output Y1,
  output Y2,
  output Y3,
  output Y4,
  output Z1,
  output Z2,
  output Z3,
  output Z4
);

  wire not_1_out, not_2_out;

  not not_1 (not_1_out, OEA);
  not not_2 (not_2_out, OEB);
  assign Y1 = not_1_out ? A1 : 1'bz;  // Controlled_Buffer controlled_buffer_1
  assign Y2 = not_1_out ? A2 : 1'bz;  // Controlled_Buffer controlled_buffer_2
  assign Y3 = not_1_out ? A3 : 1'bz;  // Controlled_Buffer controlled_buffer_3
  assign Y4 = not_1_out ? A4 : 1'bz;  // Controlled_Buffer controlled_buffer_4
  assign Z1 = not_2_out ? B1 : 1'bz;  // Controlled_Buffer controlled_buffer_5
  assign Z2 = not_2_out ? B2 : 1'bz;  // Controlled_Buffer controlled_buffer_6
  assign Z3 = not_2_out ? B3 : 1'bz;  // Controlled_Buffer controlled_buffer_7
  assign Z4 = not_2_out ? B4 : 1'bz;  // Controlled_Buffer controlled_buffer_8
endmodule

module IC_7474_FIXED (
  input  D1,
  input  Clock1,
  input  SetN1,
  input  ClearN1,
  input  D2,
  input  Clock2,
  input  SetN2,
  input  ClearN2,
  output Q1,
  output R1,
  output Q2,
  output R2
);

  wire CLR1, CLR2;

  DIP_7404 dip_7404_1 (
    .A1(ClearN1), .A2(ClearN2), .A3(Q1), .A4(Q2), .Y1(CLR1), .Y2(CLR2), .Y3(R1), .Y4(R2));  // open: A5, A6, Y5, Y6
  Register #(.trigger("rising"), .width(1)) register_1 (.D(D1), .en(1'b1), .Q(Q1), .clk(Clock1), .clr(CLR1));
  Register #(.trigger("rising"), .width(1)) register_2 (.D(D2), .en(1'b1), .Q(Q2), .clk(Clock2), .clr(CLR2));

  // Notes on the sheet:
  //   Исправленная модель 74HC74: активный-low /CLR, фронт такта, два D-триггера
endmodule

module Register8_74xx (
  input  [7:0] D,
  input  Clock,
  input  Load,
  input  ResetN,
  output [7:0] Q
);

  wire NEXT0, NEXT1, NEXT2, NEXT3, NEXT4, NEXT5, NEXT6, NEXT7, QN0, QN1, QN2, QN3, QN4, QN5, QN6, QN7;

  DIP_74157 dip_74157_1 (
    .A1(Q[0]), .B1(D[0]), .A2(Q[1]), .B2(D[1]), .A3(Q[2]), .B3(D[2]), .A4(Q[3]), .B4(D[3]), .S0(Load),
    .OE(1'b0), .Y1(NEXT0), .Y2(NEXT1), .Y3(NEXT2), .Y4(NEXT3));
  DIP_74157 dip_74157_2 (
    .A1(Q[4]), .B1(D[4]), .A2(Q[5]), .B2(D[5]), .A3(Q[6]), .B3(D[6]), .A4(Q[7]), .B4(D[7]), .S0(Load),
    .OE(1'b0), .Y1(NEXT4), .Y2(NEXT5), .Y3(NEXT6), .Y4(NEXT7));
  IC_7474_FIXED ic_7474_fixed_1 (
    .D1(NEXT0), .Clock1(Clock), .SetN1(1'b1), .ClearN1(ResetN), .D2(NEXT1), .Clock2(Clock), .SetN2(1'b1),
    .ClearN2(ResetN), .Q1(Q[0]), .R1(QN0), .Q2(Q[1]), .R2(QN1));
  IC_7474_FIXED ic_7474_fixed_2 (
    .D1(NEXT2), .Clock1(Clock), .SetN1(1'b1), .ClearN1(ResetN), .D2(NEXT3), .Clock2(Clock), .SetN2(1'b1),
    .ClearN2(ResetN), .Q1(Q[2]), .R1(QN2), .Q2(Q[3]), .R2(QN3));
  IC_7474_FIXED ic_7474_fixed_3 (
    .D1(NEXT4), .Clock1(Clock), .SetN1(1'b1), .ClearN1(ResetN), .D2(NEXT5), .Clock2(Clock), .SetN2(1'b1),
    .ClearN2(ResetN), .Q1(Q[4]), .R1(QN4), .Q2(Q[5]), .R2(QN5));
  IC_7474_FIXED ic_7474_fixed_4 (
    .D1(NEXT6), .Clock1(Clock), .SetN1(1'b1), .ClearN1(ResetN), .D2(NEXT7), .Clock2(Clock), .SetN2(1'b1),
    .ClearN2(ResetN), .Q1(Q[6]), .R1(QN6), .Q2(Q[7]), .R2(QN7));

  // Notes on the sheet:
  //   U1/U2: 74HC157 — синхронный выбор hold/load без глитчей такта
  //   U3…U6: 74HC74 — восемь D-триггеров, /SET и /CLR подключены явно
endmodule

module Buffer8_74xx (
  input  [7:0] D,
  input  OEN,
  output [7:0] Q
);

  DIP_74244 dip_74244_1 (
    .A1(D[0]), .A2(D[1]), .A3(D[2]), .A4(D[3]), .OEA(OEN), .B1(D[4]), .B2(D[5]), .B3(D[6]), .B4(D[7]),
    .OEB(OEN), .Y1(Q[0]), .Y2(Q[1]), .Y3(Q[2]), .Y4(Q[3]), .Z1(Q[4]), .Z2(Q[5]), .Z3(Q[6]), .Z4(Q[7]));

  // Notes on the sheet:
  //   U1: 74HC244 — реальный трёхстабильный драйвер системной шины
endmodule

module And1_7408 (
  input  A,
  input  B,
  output Y
);

  DIP_7408 dip_7408_1 (.A1(A), .B1(B), .Y1(Y));  // open: A2, B2, A3, B3, A4, B4, Y2, Y3, Y4
endmodule

module FFTest_7474 (
  input  D,
  input  Clock,
  input  SetN,
  input  ClearN,
  output Q,
  output QN
);

  wire Q2, QN2;

  IC_7474_FIXED ic_7474_fixed_1 (
    .D1(D), .Clock1(Clock), .SetN1(SetN), .ClearN1(ClearN), .D2(D), .Clock2(Clock), .SetN2(SetN),
    .ClearN2(ClearN), .Q1(Q), .R1(QN), .Q2(Q2), .R2(QN2));
endmodule

module PC8_74xx (
  input  [7:0] D,
  input  Clock,
  input  ResetN,
  input  Inc,
  input  LoadN,
  output [7:0] Q
);

  wire C1, C2, C3, C4, C5, C6, C7, C8, IQ0, IQ1, IQ2, IQ3, IQ4, IQ5, IQ6, IQ7, NEXT0, NEXT1, NEXT2, NEXT3,
       NEXT4, NEXT5, NEXT6, NEXT7, QN0, QN1, QN2, QN3, QN4, QN5, QN6, QN7;

  DIP_7486 dip_7486_1 (
    .A1(Q[0]), .B1(Inc), .A2(Q[1]), .B2(C1), .A3(Q[2]), .B3(C2), .A4(Q[3]), .B4(C3), .Y1(IQ0), .Y2(IQ1),
    .Y3(IQ2), .Y4(IQ3));
  DIP_7486 dip_7486_2 (
    .A1(Q[4]), .B1(C4), .A2(Q[5]), .B2(C5), .A3(Q[6]), .B3(C6), .A4(Q[7]), .B4(C7), .Y1(IQ4), .Y2(IQ5),
    .Y3(IQ6), .Y4(IQ7));
  DIP_7408 dip_7408_1 (
    .A1(Q[0]), .B1(Inc), .A2(Q[1]), .B2(C1), .A3(Q[2]), .B3(C2), .A4(Q[3]), .B4(C3), .Y1(C1), .Y2(C2),
    .Y3(C3), .Y4(C4));
  DIP_7408 dip_7408_2 (
    .A1(Q[4]), .B1(C4), .A2(Q[5]), .B2(C5), .A3(Q[6]), .B3(C6), .A4(Q[7]), .B4(C7), .Y1(C5), .Y2(C6),
    .Y3(C7), .Y4(C8));
  DIP_74157 dip_74157_1 (
    .A1(D[0]), .B1(IQ0), .A2(D[1]), .B2(IQ1), .A3(D[2]), .B3(IQ2), .A4(D[3]), .B4(IQ3), .S0(LoadN),
    .OE(1'b0), .Y1(NEXT0), .Y2(NEXT1), .Y3(NEXT2), .Y4(NEXT3));
  DIP_74157 dip_74157_2 (
    .A1(D[4]), .B1(IQ4), .A2(D[5]), .B2(IQ5), .A3(D[6]), .B3(IQ6), .A4(D[7]), .B4(IQ7), .S0(LoadN),
    .OE(1'b0), .Y1(NEXT4), .Y2(NEXT5), .Y3(NEXT6), .Y4(NEXT7));
  IC_7474_FIXED ic_7474_fixed_1 (
    .D1(NEXT0), .Clock1(Clock), .SetN1(1'b1), .ClearN1(ResetN), .D2(NEXT1), .Clock2(Clock), .SetN2(1'b1),
    .ClearN2(ResetN), .Q1(Q[0]), .R1(QN0), .Q2(Q[1]), .R2(QN1));
  IC_7474_FIXED ic_7474_fixed_2 (
    .D1(NEXT2), .Clock1(Clock), .SetN1(1'b1), .ClearN1(ResetN), .D2(NEXT3), .Clock2(Clock), .SetN2(1'b1),
    .ClearN2(ResetN), .Q1(Q[2]), .R1(QN2), .Q2(Q[3]), .R2(QN3));
  IC_7474_FIXED ic_7474_fixed_3 (
    .D1(NEXT4), .Clock1(Clock), .SetN1(1'b1), .ClearN1(ResetN), .D2(NEXT5), .Clock2(Clock), .SetN2(1'b1),
    .ClearN2(ResetN), .Q1(Q[4]), .R1(QN4), .Q2(Q[5]), .R2(QN5));
  IC_7474_FIXED ic_7474_fixed_4 (
    .D1(NEXT6), .Clock1(Clock), .SetN1(1'b1), .ClearN1(ResetN), .D2(NEXT7), .Clock2(Clock), .SetN2(1'b1),
    .ClearN2(ResetN), .Q1(Q[6]), .R1(QN6), .Q2(Q[7]), .R2(QN7));

  // Notes on the sheet:
  //   Счётчик команд: восьмибитный инкрементатор + MUX загрузки + регистр 74xx
endmodule

module StepCounter_74xx (
  input  Clock,
  input  ResetN,
  input  Run,
  input  LoadN,
  output [2:0] Step
);

  wire S3, S4, S5, S6, S7;

  PC8_74xx pc8_74xx_1 (
    .D({8{1'b0}}), .Clock(Clock), .ResetN(ResetN), .Inc(Run), .LoadN(LoadN), .Q({S7, S6, S5, S4, S3, Step}));

  // Other names for the same wires on the sheet: S0 = Step[0]; Step8[7:0] = {S7, S6, S5, S4, S3, Step}; S1 = Step[1];
  //   S2 = Step[2]
endmodule

module Flags_74xx (
  input  ZeroIn,
  input  CarryIn,
  input  Clock,
  input  Load,
  input  ResetN,
  output Zero,
  output Carry
);

  wire CarryN, CarryNext, ZeroN, ZeroNext;

  DIP_74157 dip_74157_1 (
    .A1(Zero), .B1(ZeroIn), .A2(Carry), .B2(CarryIn), .S0(Load), .OE(1'b0), .Y1(ZeroNext), .Y2(CarryNext));  // open: A3, B3, A4, B4, Y3, Y4
  IC_7474_FIXED ic_7474_fixed_1 (
    .D1(ZeroNext), .Clock1(Clock), .SetN1(1'b1), .ClearN1(ResetN), .D2(CarryNext), .Clock2(Clock),
    .SetN2(1'b1), .ClearN2(ResetN), .Q1(Zero), .R1(ZeroN), .Q2(Carry), .R2(CarryN));
endmodule

module HaltLatch_74xx (
  input  Clock,
  input  SetHalt,
  input  ResetN,
  output Halt,
  output Run
);

  wire HaltNext, UnusedQ, UnusedQN;

  DIP_7432 dip_7432_1 (.A1(Halt), .B1(SetHalt), .Y1(HaltNext));  // open: A2, B2, A3, B3, A4, B4, Y2, Y3, Y4
  IC_7474_FIXED ic_7474_fixed_1 (
    .D1(HaltNext), .Clock1(Clock), .SetN1(1'b1), .ClearN1(ResetN), .D2(1'b0), .Clock2(1'b0), .SetN2(1'b1),
    .ClearN2(ResetN), .Q1(Halt), .R1(Run), .Q2(UnusedQ), .R2(UnusedQN));
endmodule

module ALU8_74xx (
  input  [7:0] A,
  input  [7:0] B,
  input  [1:0] Sel,
  input  Sub,
  output [7:0] Q,
  output Carry,
  output Zero
);

  wire ADD0, ADD1, ADD2, ADD3, ADD4, ADD5, ADD6, ADD7, AND0, AND1, AND2, AND3, AND4, AND5, AND6, AND7, BX0,
       BX1, BX2, BX3, BX4, BX5, BX6, BX7, C1, C2, C3, C4, C5, C6, C7, G0, G1, G2, G3, G4, G5, G6, G7, H0, H1,
       H2, H3, H4, H5, H6, H7, M00, M01, M02, M03, M04, M05, M06, M07, M10, M11, M12, M13, M14, M15, M16,
       M17, NQ0, NQ1, NQ2, NQ3, NQ4, NQ5, NQ6, NQ7, OR0, OR1, OR2, OR3, OR4, OR5, OR6, OR7, P0, P1, P2, P3,
       P4, P5, P6, P7, XOR0, XOR1, XOR2, XOR3, XOR4, XOR5, XOR6, XOR7, ZeroN;

  DIP_7486 dip_7486_1 (
    .A1(B[0]), .B1(Sub), .A2(B[1]), .B2(Sub), .A3(B[2]), .B3(Sub), .A4(B[3]), .B4(Sub), .Y1(BX0), .Y2(BX1),
    .Y3(BX2), .Y4(BX3));
  DIP_7486 dip_7486_2 (
    .A1(B[4]), .B1(Sub), .A2(B[5]), .B2(Sub), .A3(B[6]), .B3(Sub), .A4(B[7]), .B4(Sub), .Y1(BX4), .Y2(BX5),
    .Y3(BX6), .Y4(BX7));
  DIP_7486 dip_7486_3 (
    .A1(A[0]), .B1(BX0), .A2(A[1]), .B2(BX1), .A3(A[2]), .B3(BX2), .A4(A[3]), .B4(BX3), .Y1(P0), .Y2(P1),
    .Y3(P2), .Y4(P3));
  DIP_7486 dip_7486_4 (
    .A1(A[4]), .B1(BX4), .A2(A[5]), .B2(BX5), .A3(A[6]), .B3(BX6), .A4(A[7]), .B4(BX7), .Y1(P4), .Y2(P5),
    .Y3(P6), .Y4(P7));
  DIP_7408 dip_7408_1 (
    .A1(A[0]), .B1(BX0), .A2(A[1]), .B2(BX1), .A3(A[2]), .B3(BX2), .A4(A[3]), .B4(BX3), .Y1(G0), .Y2(G1),
    .Y3(G2), .Y4(G3));
  DIP_7408 dip_7408_2 (
    .A1(A[4]), .B1(BX4), .A2(A[5]), .B2(BX5), .A3(A[6]), .B3(BX6), .A4(A[7]), .B4(BX7), .Y1(G4), .Y2(G5),
    .Y3(G6), .Y4(G7));
  DIP_7486 dip_7486_5 (
    .A1(P0), .B1(Sub), .A2(P1), .B2(C1), .A3(P2), .B3(C2), .A4(P3), .B4(C3), .Y1(ADD0), .Y2(ADD1), .Y3(ADD2),
    .Y4(ADD3));
  DIP_7486 dip_7486_6 (
    .A1(P4), .B1(C4), .A2(P5), .B2(C5), .A3(P6), .B3(C6), .A4(P7), .B4(C7), .Y1(ADD4), .Y2(ADD5), .Y3(ADD6),
    .Y4(ADD7));
  DIP_7408 dip_7408_3 (
    .A1(P0), .B1(Sub), .A2(P1), .B2(C1), .A3(P2), .B3(C2), .A4(P3), .B4(C3), .Y1(H0), .Y2(H1), .Y3(H2),
    .Y4(H3));
  DIP_7408 dip_7408_4 (
    .A1(P4), .B1(C4), .A2(P5), .B2(C5), .A3(P6), .B3(C6), .A4(P7), .B4(C7), .Y1(H4), .Y2(H5), .Y3(H6), .Y4(H7));
  DIP_7432 dip_7432_1 (
    .A1(G0), .B1(H0), .A2(G1), .B2(H1), .A3(G2), .B3(H2), .A4(G3), .B4(H3), .Y1(C1), .Y2(C2), .Y3(C3), .Y4(C4));
  DIP_7432 dip_7432_2 (
    .A1(G4), .B1(H4), .A2(G5), .B2(H5), .A3(G6), .B3(H6), .A4(G7), .B4(H7), .Y1(C5), .Y2(C6), .Y3(C7),
    .Y4(Carry));
  DIP_7408 dip_7408_5 (
    .A1(A[0]), .B1(B[0]), .A2(A[1]), .B2(B[1]), .A3(A[2]), .B3(B[2]), .A4(A[3]), .B4(B[3]), .Y1(AND0),
    .Y2(AND1), .Y3(AND2), .Y4(AND3));
  DIP_7408 dip_7408_6 (
    .A1(A[4]), .B1(B[4]), .A2(A[5]), .B2(B[5]), .A3(A[6]), .B3(B[6]), .A4(A[7]), .B4(B[7]), .Y1(AND4),
    .Y2(AND5), .Y3(AND6), .Y4(AND7));
  DIP_7432 dip_7432_3 (
    .A1(A[0]), .B1(B[0]), .A2(A[1]), .B2(B[1]), .A3(A[2]), .B3(B[2]), .A4(A[3]), .B4(B[3]), .Y1(OR0),
    .Y2(OR1), .Y3(OR2), .Y4(OR3));
  DIP_7432 dip_7432_4 (
    .A1(A[4]), .B1(B[4]), .A2(A[5]), .B2(B[5]), .A3(A[6]), .B3(B[6]), .A4(A[7]), .B4(B[7]), .Y1(OR4),
    .Y2(OR5), .Y3(OR6), .Y4(OR7));
  DIP_7486 dip_7486_7 (
    .A1(A[0]), .B1(B[0]), .A2(A[1]), .B2(B[1]), .A3(A[2]), .B3(B[2]), .A4(A[3]), .B4(B[3]), .Y1(XOR0),
    .Y2(XOR1), .Y3(XOR2), .Y4(XOR3));
  DIP_7486 dip_7486_8 (
    .A1(A[4]), .B1(B[4]), .A2(A[5]), .B2(B[5]), .A3(A[6]), .B3(B[6]), .A4(A[7]), .B4(B[7]), .Y1(XOR4),
    .Y2(XOR5), .Y3(XOR6), .Y4(XOR7));
  DIP_74157 dip_74157_1 (
    .A1(ADD0), .B1(AND0), .A2(ADD1), .B2(AND1), .A3(ADD2), .B3(AND2), .A4(ADD3), .B4(AND3), .S0(Sel[0]),
    .OE(1'b0), .Y1(M00), .Y2(M01), .Y3(M02), .Y4(M03));
  DIP_74157 dip_74157_2 (
    .A1(ADD4), .B1(AND4), .A2(ADD5), .B2(AND5), .A3(ADD6), .B3(AND6), .A4(ADD7), .B4(AND7), .S0(Sel[0]),
    .OE(1'b0), .Y1(M04), .Y2(M05), .Y3(M06), .Y4(M07));
  DIP_7404 dip_7404_1 (
    .A1(Q[0]), .A2(Q[1]), .A3(Q[2]), .A4(Q[3]), .A5(Q[4]), .A6(Q[5]), .Y1(NQ0), .Y2(NQ1), .Y3(NQ2), .Y4(NQ3),
    .Y5(NQ4), .Y6(NQ5));
  DIP_74157 dip_74157_3 (
    .A1(OR0), .B1(XOR0), .A2(OR1), .B2(XOR1), .A3(OR2), .B3(XOR2), .A4(OR3), .B4(XOR3), .S0(Sel[0]),
    .OE(1'b0), .Y1(M10), .Y2(M11), .Y3(M12), .Y4(M13));
  DIP_74157 dip_74157_4 (
    .A1(OR4), .B1(XOR4), .A2(OR5), .B2(XOR5), .A3(OR6), .B3(XOR6), .A4(OR7), .B4(XOR7), .S0(Sel[0]),
    .OE(1'b0), .Y1(M14), .Y2(M15), .Y3(M16), .Y4(M17));
  DIP_7404 dip_7404_2 (
    .A1(Q[6]), .A2(Q[7]), .A3(ZeroN), .Y1(NQ6), .Y2(NQ7), .Y3(Zero));  // open: A4, A5, A6, Y4, Y5, Y6
  DIP_74157 dip_74157_5 (
    .A1(M00), .B1(M10), .A2(M01), .B2(M11), .A3(M02), .B3(M12), .A4(M03), .B4(M13), .S0(Sel[1]), .OE(1'b0),
    .Y1(Q[0]), .Y2(Q[1]), .Y3(Q[2]), .Y4(Q[3]));
  DIP_74157 dip_74157_6 (
    .A1(M04), .B1(M14), .A2(M05), .B2(M15), .A3(M06), .B3(M16), .A4(M07), .B4(M17), .S0(Sel[1]), .OE(1'b0),
    .Y1(Q[4]), .Y2(Q[5]), .Y3(Q[6]), .Y4(Q[7]));
  DIP_7430 dip_7430_1 (.A(NQ0), .B(NQ1), .C(NQ2), .D(NQ3), .E(NQ4), .F(NQ5), .G(NQ6), .H(NQ7), .Y(ZeroN));

  // Other names for the same wires on the sheet: C8 = Carry

  // Notes on the sheet:
  //   ADD/SUB: каскад полных сумматоров 7486/7408/7432; AND/OR/XOR: 7408/7432/7486
  //   Выбор операции: 6×74157; детектор нуля: 2×7404 + 7430
endmodule

module ControlStore_28C64 (
  input  [3:0] Opcode,
  input  [2:0] Step,
  input  Zero,
  input  Carry,
  input  Halt,
  output [19:0] Control
);

  ROM #(.addrWidth(10), .dataWidth(20)) AT28C64_CONTROL (.addr({Halt, Carry, Zero, Opcode, Step}), .data(Control));
  // Pins of 9 and 10 bits meet at {Halt, Carry, Zero, Opcode, Step}

  // Other names for the same wires on the sheet: UA0 = Step[0]; UADDR[9:0] = {Halt, Carry, Zero, Opcode, Step};
  //   UA1 = Step[1]; UA2 = Step[2]; UA3 = Opcode[0]; UA4 = Opcode[1]; UA5 = Opcode[2]; UA6 = Opcode[3]; UA7 = Zero;
  //   UA8 = Carry; UA9 = Halt

  // Notes on the sheet:
  //   Адрес: HALT, C, Z, opcode[3:0], microstep[2:0]
  //   20 управляющих линий; содержимое ПЗУ формируется генератором
  //   contents of AT28C64_CONTROL (hex, n*v repeats v):
  //   04cba 04cbc 00cb1 04cb1 04cb1 04cb1 04cb1 04cb1 04cba 04cbc 009b1 04cb1 04cb1 04cb1 04cb1 04cb1
  //   04cba 04cbc 00d91 04cb1 04cb1 04cb1 04cb1 04cb1 04cba 04cbc 00c71 04cb1 04cb1 04cb1 04cb1 04cb1
  //   04cba 04cbc 04e91 015b1 04cb1 04cb1 04cb1 04cb1 04cba 04cbc 04e91 415b1 04cb1 04cb1 04cb1 04cb1
  //   04cba 04cbc 04e91 115b1 04cb1 04cb1 04cb1 04cb1 04cba 04cbc 04e91 215b1 04cb1 04cb1 04cb1 04cb1
  //   04cba 04cbc 04e91 315b1 04cb1 04cb1 04cb1 04cb1 04cba 04cbc 00ca1 04cb1 04cb1 04cb1 04cb1 04cb1
  //   04cba 04cbc 00cb1 04cb1 04cb1 04cb1 04cb1 04cb1 04cba 04cbc 00cb1 04cb1 04cb1 04cb1 04cb1 04cb1
  //   04cba 04cbc 02c31 04cb1 04cb1 04cb1 04cb1 04cb1 04cba 04cbc 00cb1 04cb1 04cb1 04cb1 04cb1 04cb1
  //   04cba 04cbc 00cb1 04cb1 04cb1 04cb1 04cb1 04cb1 04cba 04cbc 08cb1 04cb1 04cb1 04cb1 04cb1 04cb1
  //   04cba 04cbc 00cb1 04cb1 04cb1 04cb1 04cb1 04cb1 04cba 04cbc 009b1 04cb1 04cb1 04cb1 04cb1 04cb1
  //   04cba 04cbc 00d91 04cb1 04cb1 04cb1 04cb1 04cb1 04cba 04cbc 00c71 04cb1 04cb1 04cb1 04cb1 04cb1
  //   04cba 04cbc 04e91 015b1 04cb1 04cb1 04cb1 04cb1 04cba 04cbc 04e91 415b1 04cb1 04cb1 04cb1 04cb1
  //   04cba 04cbc 04e91 115b1 04cb1 04cb1 04cb1 04cb1 04cba 04cbc 04e91 215b1 04cb1 04cb1 04cb1 04cb1
  //   04cba 04cbc 04e91 315b1 04cb1 04cb1 04cb1 04cb1 04cba 04cbc 00ca1 04cb1 04cb1 04cb1 04cb1 04cb1
  //   04cba 04cbc 00ca1 04cb1 04cb1 04cb1 04cb1 04cb1 04cba 04cbc 00cb1 04cb1 04cb1 04cb1 04cb1 04cb1
  //   04cba 04cbc 02c31 04cb1 04cb1 04cb1 04cb1 04cb1 04cba 04cbc 00cb1 04cb1 04cb1 04cb1 04cb1 04cb1
  //   04cba 04cbc 00cb1 04cb1 04cb1 04cb1 04cb1 04cb1 04cba 04cbc 08cb1 04cb1 04cb1 04cb1 04cb1 04cb1
  //   04cba 04cbc 00cb1 04cb1 04cb1 04cb1 04cb1 04cb1 04cba 04cbc 009b1 04cb1 04cb1 04cb1 04cb1 04cb1
  //   04cba 04cbc 00d91 04cb1 04cb1 04cb1 04cb1 04cb1 04cba 04cbc 00c71 04cb1 04cb1 04cb1 04cb1 04cb1
  //   04cba 04cbc 04e91 015b1 04cb1 04cb1 04cb1 04cb1 04cba 04cbc 04e91 415b1 04cb1 04cb1 04cb1 04cb1
  //   04cba 04cbc 04e91 115b1 04cb1 04cb1 04cb1 04cb1 04cba 04cbc 04e91 215b1 04cb1 04cb1 04cb1 04cb1
  //   04cba 04cbc 04e91 315b1 04cb1 04cb1 04cb1 04cb1 04cba 04cbc 00ca1 04cb1 04cb1 04cb1 04cb1 04cb1
  //   04cba 04cbc 00cb1 04cb1 04cb1 04cb1 04cb1 04cb1 04cba 04cbc 00ca1 04cb1 04cb1 04cb1 04cb1 04cb1
  //   04cba 04cbc 02c31 04cb1 04cb1 04cb1 04cb1 04cb1 04cba 04cbc 00cb1 04cb1 04cb1 04cb1 04cb1 04cb1
  //   04cba 04cbc 00cb1 04cb1 04cb1 04cb1 04cb1 04cb1 04cba 04cbc 08cb1 04cb1 04cb1 04cb1 04cb1 04cb1
  //   04cba 04cbc 00cb1 04cb1 04cb1 04cb1 04cb1 04cb1 04cba 04cbc 009b1 04cb1 04cb1 04cb1 04cb1 04cb1
  //   04cba 04cbc 00d91 04cb1 04cb1 04cb1 04cb1 04cb1 04cba 04cbc 00c71 04cb1 04cb1 04cb1 04cb1 04cb1
  //   04cba 04cbc 04e91 015b1 04cb1 04cb1 04cb1 04cb1 04cba 04cbc 04e91 415b1 04cb1 04cb1 04cb1 04cb1
  //   04cba 04cbc 04e91 115b1 04cb1 04cb1 04cb1 04cb1 04cba 04cbc 04e91 215b1 04cb1 04cb1 04cb1 04cb1
  //   04cba 04cbc 04e91 315b1 04cb1 04cb1 04cb1 04cb1 04cba 04cbc 00ca1 04cb1 04cb1 04cb1 04cb1 04cb1
  //   04cba 04cbc 00ca1 04cb1 04cb1 04cb1 04cb1 04cb1 04cba 04cbc 00ca1 04cb1 04cb1 04cb1 04cb1 04cb1
  //   04cba 04cbc 02c31 04cb1 04cb1 04cb1 04cb1 04cb1 04cba 04cbc 00cb1 04cb1 04cb1 04cb1 04cb1 04cb1
  //   04cba 04cbc 00cb1 04cb1 04cb1 04cb1 04cb1 04cb1 04cba 04cbc 08cb1 04cb1 04cb1 04cb1 04cb1 04cb1
  //   00cb1 00cb1 00cb1 00cb1 00cb1 00cb1 00cb1 00cb1 00cb1 00cb1 00cb1 00cb1 00cb1 00cb1 00cb1 00cb1
  //   00cb1 00cb1 00cb1 00cb1 00cb1 00cb1 00cb1 00cb1 00cb1 00cb1 00cb1 00cb1 00cb1 00cb1 00cb1 00cb1
  //   00cb1 00cb1 00cb1 00cb1 00cb1 00cb1 00cb1 00cb1 00cb1 00cb1 00cb1 00cb1 00cb1 00cb1 00cb1 00cb1
  //   00cb1 00cb1 00cb1 00cb1 00cb1 00cb1 00cb1 00cb1 00cb1 00cb1 00cb1 00cb1 00cb1 00cb1 00cb1 00cb1
  //   00cb1 00cb1 00cb1 00cb1 00cb1 00cb1 00cb1 00cb1 00cb1 00cb1 00cb1 00cb1 00cb1 00cb1 00cb1 00cb1
  //   00cb1 00cb1 00cb1 00cb1 00cb1 00cb1 00cb1 00cb1 00cb1 00cb1 00cb1 00cb1 00cb1 00cb1 00cb1 00cb1
  //   00cb1 00cb1 00cb1 00cb1 00cb1 00cb1 00cb1 00cb1 00cb1 00cb1 00cb1 00cb1 00cb1 00cb1 00cb1 00cb1
  //   00cb1 00cb1 00cb1 00cb1 00cb1 00cb1 00cb1 00cb1 00cb1 00cb1 00cb1 00cb1 00cb1 00cb1 00cb1 00cb1
  //   00cb1 00cb1 00cb1 00cb1 00cb1 00cb1 00cb1 00cb1 00cb1 00cb1 00cb1 00cb1 00cb1 00cb1 00cb1 00cb1
  //   00cb1 00cb1 00cb1 00cb1 00cb1 00cb1 00cb1 00cb1 00cb1 00cb1 00cb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
endmodule

module ProgramROM_28C16 (
  input  [7:0] Address,
  output [7:0] Data
);

  ROM #(.addrWidth(8), .dataWidth(8)) AT28C16_PROGRAM (.addr(Address), .data(Data));

  // Notes on the sheet:
  //   В ПЗУ уже записана демонстрационная программа
  //   contents of AT28C16_PROGRAM (hex, n*v repeats v):
  //   01 05 03 20 01 fa 04 20 04 20 0b 0e 01 63 09 10 01 2a 05 20 08 20 07 20 06 20 05 20 0a 20 01 63 0c
  //   00 0f 00 00 00 00 00 00 00 00 00 00 00 00 00 00 00 00 00 00 00 00 00 00 00 00 00 00 00 00 00 00 00
  //   00 00 00 00 00 00 00 00 00 00 00 00 00 00 00 00 00 00 00 00 00 00 00 00 00 00 00 00 00 00 00 00 00
  //   00 00 00 00 00 00 00 00 00 00 00 00 00 00 00 00 00 00 00 00 00 00 00 00 00 00 00 00 00 00 00 00 00
  //   00 00 00 00 00 00 00 00 00 00 00 00 00 00 00 00 00 00 00 00 00 00 00 00 00 00 00 00 00 00 00 00 00
  //   00 00 00 00 00 00 00 00 00 00 00 00 00 00 00 00 00 00 00 00 00 00 00 00 00 00 00 00 00 00 00 00 00
  //   00 00 00 00 00 00 00 00 00 00 00 00 00 00 00 00 00 00 00 00 00 00 00 00 00 00 00 00 00 00 00 00 00
  //   00 00 00 00 00 00 00 00 00 00 00 00 00 00 00 00 00 00 00 00 00 00 00 00 00
endmodule

module DataRAM_62256 (
  input  [7:0] Address,
  input  [7:0] DataIn,
  input  Clock,
  input  WE,
  output [7:0] DataOut
);

  RAM #(.addrWidth(8), .asyncread("true"), .byteenables("NobyteEnables"), .dataWidth(8), .databus("bibus"), .enables("byte"), .trigger("rising")) _62256_SRAM (
    .addr(Address), .we(WE), .oe(1'b1), .clk(Clock), .din(DataIn), .dout(DataOut));

  // Notes on the sheet:
  //   В симуляторе — RAM; на макете — SRAM 62256 (используются A0…A7)
endmodule

module CPU7400_Core (
  input  Clock,
  input  ResetN,
  output [7:0] Out,
  output Halt,
  output [7:0] PC,
  output [7:0] A,
  output [2:0] Step
);

  wire A_LOAD, A_OEN, ALU_C, ALU_OEN, ALU_Z, B_LOAD, CarryFlag, Run, ZeroFlag;
  wire [1:0] ALU_SEL;
  wire [7:0] ALU_Q, B, BUS, IR, Operand, ProgramData, RAM_DATA;
  wire [19:0] Control;

  HaltLatch_74xx haltlatch_74xx_1 (.Clock(Clock), .SetHalt(Control[15]), .ResetN(ResetN), .Halt(Halt), .Run(Run));
  StepCounter_74xx stepcounter_74xx_1 (.Clock(Clock), .ResetN(ResetN), .Run(Run), .LoadN(Control[14]), .Step(Step));
  PC8_74xx pc8_74xx_1 (.D(Operand), .Clock(Clock), .ResetN(ResetN), .Inc(Control[3]), .LoadN(Control[4]), .Q(PC));
  ProgramROM_28C16 programrom_28c16_1 (.Address(PC), .Data(ProgramData));
  Buffer8_74xx buffer8_74xx_1 (.D(ProgramData), .OEN(Control[0]), .Q(BUS));
  Register8_74xx register8_74xx_1 (.D(BUS), .Clock(Clock), .Load(A_LOAD), .ResetN(ResetN), .Q(A));
  Register8_74xx register8_74xx_2 (.D(BUS), .Clock(Clock), .Load(B_LOAD), .ResetN(ResetN), .Q(B));
  Register8_74xx register8_74xx_3 (.D(BUS), .Clock(Clock), .Load(Control[1]), .ResetN(ResetN), .Q(IR));
  Register8_74xx register8_74xx_4 (.D(BUS), .Clock(Clock), .Load(Control[2]), .ResetN(ResetN), .Q(Operand));
  Buffer8_74xx buffer8_74xx_2 (.D(Operand), .OEN(Control[10]), .Q(BUS));
  ALU8_74xx alu8_74xx_1 (.A(A), .B(B), .Sel(ALU_SEL), .Sub(Control[18]), .Q(ALU_Q), .Carry(ALU_C), .Zero(ALU_Z));
  DataRAM_62256 dataram_62256_1 (.Address(Operand), .DataIn(BUS), .Clock(Clock), .WE(Control[6]), .DataOut(RAM_DATA));
  Buffer8_74xx buffer8_74xx_3 (.D(ALU_Q), .OEN(ALU_OEN), .Q(BUS));
  Buffer8_74xx buffer8_74xx_4 (.D(RAM_DATA), .OEN(Control[5]), .Q(BUS));
  ControlStore_28C64 controlstore_28c64_1 (
    .Opcode(IR[3:0]), .Step(Step), .Zero(ZeroFlag), .Carry(CarryFlag), .Halt(Halt),
    .Control({Control[19:18], ALU_SEL, Control[15:12], ALU_OEN, Control[10], B_LOAD, A_LOAD, A_OEN, Control[6:0]}));
  Flags_74xx flags_74xx_1 (
    .ZeroIn(ALU_Z), .CarryIn(ALU_C), .Clock(Clock), .Load(Control[12]), .ResetN(ResetN), .Zero(ZeroFlag),
    .Carry(CarryFlag));
  Buffer8_74xx buffer8_74xx_5 (.D(A), .OEN(A_OEN), .Q(BUS));
  Register8_74xx register8_74xx_5 (.D(BUS), .Clock(Clock), .Load(Control[13]), .ResetN(ResetN), .Q(Out));

  // Other names for the same wires on the sheet: Control (some bits) = {ALU_SEL, ALU_OEN, B_LOAD, A_LOAD, A_OEN};
  //   SEL0 = ALU_SEL[0]; SEL1 = ALU_SEL[1]; PGM_OEN = Control[0]; IR_LOAD = Control[1]; OP_LOAD = Control[2];
  //   PC_INC = Control[3]; PC_LOADN = Control[4]; RAM_OEN = Control[5]; RAM_WE = Control[6]; OP_OEN = Control[10];
  //   FLAGS_LOAD = Control[12]; OUT_LOAD = Control[13]; STEP_LOADN = Control[14]; HALT_SET = Control[15];
  //   SUB = Control[18]; CTRL19 = Control[19]; Opcode[3:0] = IR[3:0]

  // Notes on the sheet:
  //   СИСТЕМНАЯ ШИНА D7…D0 — источники подключены только через 74HC244
  //   ТРАКТ ДАННЫХ
  //   ПАМЯТЬ
  //   УПРАВЛЕНИЕ
endmodule

module \ЭВМ_7400  (
);

  wire Clock, Halt, ResetButton, ResetN;
  wire [2:0] Step;
  wire [7:0] A, Out, PC;

  Clock #(.highDuration(1), .lowDuration(1)) MASTER_CLOCK (.out(Clock));
  Button RESET (.out(ResetButton));
  DIP_7404 dip_7404_1 (.A1(ResetButton), .Y1(ResetN));  // open: A2, A3, A4, A5, A6, Y2, Y3, Y4, Y5, Y6
  CPU7400_Core cpu7400_core_1 (.Clock(Clock), .ResetN(ResetN), .Out(Out), .Halt(Halt), .PC(PC), .A(A), .Step(Step));
  Hex_Digit_Display hex_digit_display_1 (.value(Out[3:0]));  // open: dp
  LED u_HALT (.in(Halt));
  // Probe on Out
  // Probe on PC
  // Probe on A
  // Probe on Step
  // Pins of 4 and 8 bits meet at Out

  // Notes on the sheet:
  //   ЭВМ НА РЕАЛЬНЫХ МИКРОСХЕМАХ СЕРИИ 74xx
  //   1) Нажмите RESET  2) Включите Simulate → Ticks Enabled
  //   Демонстрация проверяет: LDI, STA, ADD, JC, JMP, SUB, XOR, OR, AND, JZ, OUT, HLT
  //   Ожидаемый результат OUT = 0, потому что финальная ветка проверяет нулевой результат
  //   Откройте CPU7400_Core для архитектуры; ALU8_74xx/PC8_74xx — для разводки корпусов
endmodule
