// Logisim project ЭВМ.circ as structural Verilog: 1 circuit, main circuit main
module main (
  input  [2:0] _011,
  input  [2:0] _011_2,
  input  [2:0] _100,
  input  [2:0] _011_3,
  input  [2:0] _011_4,
  input  [2:0] _011_5,
  input  [7:0] in_7,
  input  [7:0] in_8,
  input  [7:0] in_9,
  input  [7:0] in_10,
  input  [7:0] in_11,
  input  [7:0] in_12,
  input  [7:0] in_13,
  input  [7:0] in_14,
  input  [7:0] in_15,
  input  [7:0] in_16,
  input  [7:0] in_17,
  input  [7:0] in_18,
  input  [7:0] in_19,
  input  [7:0] in_20,
  input  [7:0] _00000010,
  input  [7:0] _00000000
);

  wire and_1_out, and_2_out, and_3_out, and_4_out, and_5_out, and_6_out, button_1_out, clock_1_out,
       comparator_1_eq, comparator_2_eq, comparator_3_eq, comparator_4_eq, comparator_5_eq, comparator_6_eq,
       comparator_7_eq, comparator_8_eq, comparator_9_eq, comparator_10_eq, comparator_11_eq,
       comparator_12_eq, comparator_13_eq, comparator_14_eq, comparator_15_eq, comparator_15_gt,
       comparator_15_lt, comparator_16_eq, comparator_17_eq, comparator_18_eq, comparator_19_eq,
       controlled_buffer_2_out, controlled_buffer_7_out, controlled_buffer_12_out, controlled_buffer_19_out,
       d_ff_1_q, d_ff_2_q, d_ff_3_q, demultiplexer_1_out1, demultiplexer_1_out2, demultiplexer_1_out3,
       nor_1_out, nor_2_out, not_1_out, not_2_out, not_3_out, or_1_out, or_2_out, or_3_out, or_4_out,
       shift_register_1_q0, shift_register_2_q0, shift_register_2_q1, shift_register_3_q0,
       shift_register_3_q1, shift_register_4_q0;
  wire [2:0] counter_2_q, register_5_q;
  wire [7:0] adder_1_out, adder_2_out, adder_3_out, adder_4_out, controlled_buffer_1_out,
       controlled_buffer_4_out, controlled_buffer_6_out, controlled_buffer_10_out, controlled_buffer_15_out,
       controlled_buffer_21_out, counter_1_q, counter_3_q, divider_1_out, multiplexer_1_out,
       multiplier_1_out, ram_1_data, register_1_q, register_2_q, register_3_q, register_4_q, register_6_q,
       rom_1_data, shifter_1_out, shifter_2_out, subtractor_1_out, subtractor_2_out, subtractor_3_out;
  wire [7:3] register_5_q_2;

  Adder adder_1 (.a(counter_1_q), .b(_00000010), .out(adder_1_out));  // open: cin, cout
  assign controlled_buffer_1_out = and_4_out ? adder_1_out : 8'bz;  // Controlled_Buffer controlled_buffer_1
  assign controlled_buffer_2_out = and_4_out ? and_4_out : 1'bz;  // Controlled_Buffer controlled_buffer_2
  assign controlled_buffer_2_out = shift_register_4_q0 ? shift_register_4_q0 : 1'bz;  // Controlled_Buffer controlled_buffer_3
  not not_1 (not_1_out, controlled_buffer_2_out);
  Counter counter_1 (
    .load(controlled_buffer_2_out), .D(controlled_buffer_1_out), .count(not_1_out), .Q(counter_1_q),
    .clk(button_1_out));  // open: carry, clr
  Button button_1 (.out(button_1_out));
  // Probe on counter_1_q
  ROM rom_1 (.addr(counter_1_q), .data(rom_1_data));  // open: sel
  // Probe on rom_1_data
  not not_2 (not_2_out, or_2_out);
  assign controlled_buffer_4_out = or_2_out ? _00000000 : 8'bz;  // Controlled_Buffer controlled_buffer_4
  assign controlled_buffer_4_out = not_2_out ? rom_1_data : 8'bz;  // Controlled_Buffer controlled_buffer_5
  assign controlled_buffer_6_out = or_2_out ? rom_1_data : 8'bz;  // Controlled_Buffer controlled_buffer_6
  Comparator comparator_1 (.a(controlled_buffer_4_out), .b(in_20), .eq(comparator_1_eq));  // open: gt, lt
  Comparator comparator_2 (.a(controlled_buffer_4_out), .b(in_19), .eq(comparator_2_eq));  // open: gt, lt
  Comparator comparator_3 (.a(controlled_buffer_4_out), .b(in_17), .eq(comparator_3_eq));  // open: gt, lt
  or or_1 (or_1_out, comparator_3_eq, comparator_2_eq, comparator_1_eq);
  // Probe on in_7
  // Probe on in_8
  // Probe on in_9
  // Probe on in_10
  // Probe on in_12
  // Probe on in_13
  // Probe on in_14
  // Probe on in_16
  // Probe on in_17
  // Probe on in_19
  // Probe on in_20
  Comparator comparator_4 (.a(in_16), .b(controlled_buffer_4_out), .eq(comparator_4_eq));  // open: gt, lt
  Comparator comparator_5 (.a(controlled_buffer_4_out), .b(in_7), .eq(comparator_5_eq));  // open: gt, lt
  Comparator comparator_6 (.a(in_8), .b(controlled_buffer_4_out), .eq(comparator_6_eq));  // open: gt, lt
  Comparator comparator_7 (.a(in_9), .b(controlled_buffer_4_out), .eq(comparator_7_eq));  // open: gt, lt
  Comparator comparator_8 (.a(controlled_buffer_4_out), .b(in_10), .eq(comparator_8_eq));  // open: gt, lt
  Comparator comparator_9 (.a(controlled_buffer_4_out), .b(in_12), .eq(comparator_9_eq));  // open: gt, lt
  Comparator comparator_10 (.a(controlled_buffer_4_out), .b(in_13), .eq(comparator_10_eq));  // open: gt, lt
  Comparator comparator_11 (.a(controlled_buffer_4_out), .b(in_14), .eq(comparator_11_eq));  // open: gt, lt
  or or_2 (or_2_out, shift_register_1_q0, shift_register_4_q0, shift_register_2_q0, shift_register_3_q0);
  assign controlled_buffer_7_out = d_ff_1_q ? d_ff_1_q : 1'bz;  // Controlled_Buffer controlled_buffer_7
  D_Flip_Flop d_ff_1 (
    .clk(comparator_1_eq), .D(comparator_1_eq), .Q(d_ff_1_q), .reset(comparator_12_eq));  // open: Qn, preset, en
  D_Flip_Flop d_ff_2 (
    .clk(comparator_2_eq), .D(comparator_2_eq), .Q(d_ff_2_q), .reset(comparator_12_eq));  // open: Qn, preset, en
  assign controlled_buffer_7_out = d_ff_2_q ? d_ff_2_q : 1'bz;  // Controlled_Buffer controlled_buffer_8
  D_Flip_Flop d_ff_3 (
    .clk(comparator_3_eq), .D(comparator_3_eq), .Q(d_ff_3_q), .reset(comparator_12_eq));  // open: Qn, preset, en
  assign controlled_buffer_7_out = d_ff_3_q ? d_ff_3_q : 1'bz;  // Controlled_Buffer controlled_buffer_9
  Shift_Register shift_register_1 (
    .in(comparator_4_eq), .clk(button_1_out), .q0(shift_register_1_q0));  // open: shift, out, load, clr, d0, d1, q1, d2, q2, d3, q3, d4, q4, d5, q5, d6, q6, d7, q7
  assign controlled_buffer_10_out = shift_register_1_q0 ? controlled_buffer_6_out : 8'bz;  // Controlled_Buffer controlled_buffer_10
  Shift_Register shift_register_2 (
    .in(comparator_5_eq), .clk(button_1_out), .q0(shift_register_2_q0), .q1(shift_register_2_q1));  // open: shift, out, load, clr, d0, d1, d2, q2, d3, q3, d4, q4, d5, q5, d6, q6, d7, q7
  or or_3 (or_3_out, or_1_out, comparator_6_eq);
  Shift_Register shift_register_3 (
    .in(comparator_8_eq), .clk(button_1_out), .q0(shift_register_3_q0), .q1(shift_register_3_q1));  // open: shift, out, load, clr, d0, d1, d2, q2, d3, q3, d4, q4, d5, q5, d6, q6, d7, q7
  Shift_Register shift_register_4 (
    .in(comparator_11_eq), .clk(button_1_out), .q0(shift_register_4_q0));  // open: shift, out, load, clr, d0, d1, q1, d2, q2, d3, q3, d4, q4, d5, q5, d6, q6, d7, q7
  assign controlled_buffer_1_out = shift_register_4_q0 ? controlled_buffer_6_out : 8'bz;  // Controlled_Buffer controlled_buffer_11
  assign controlled_buffer_12_out = controlled_buffer_7_out ? button_1_out : 1'bz;  // Controlled_Buffer controlled_buffer_12
  // Probe on _100
  Comparator #(.width(3)) comparator_12 (.a(_100), .b(counter_2_q), .eq(comparator_12_eq));  // open: gt, lt
  // Probe on controlled_buffer_1_out
  Counter #(.width(3), .max('h7)) counter_2 (
    .count(1'b1), .Q(counter_2_q), .clk(controlled_buffer_12_out), .clr(comparator_12_eq));  // open: load, D, carry
  Demultiplexer #(.select(3)) demultiplexer_1 (
    .out1(demultiplexer_1_out1), .out2(demultiplexer_1_out2), .out3(demultiplexer_1_out3), .in(1'b1),
    .sel(counter_2_q));  // open: out0, out4, out5, out6, out7, en
  Register register_1 (.D(controlled_buffer_6_out), .Q(register_1_q), .clk(shift_register_2_q1));  // open: en, clr
  Register register_2 (.D(controlled_buffer_6_out), .Q(register_2_q), .clk(shift_register_3_q1));  // open: en, clr
  Adder adder_2 (.a(register_6_q), .b(register_1_q), .out(adder_2_out));  // open: cin, cout
  Subtractor subtractor_1 (.a(register_6_q), .b(register_1_q), .out(subtractor_1_out));  // open: bin, bout
  Register register_3 (
    .D(ram_1_data), .Q(register_3_q), .clk(demultiplexer_1_out2), .clr(comparator_12_eq));  // open: en
  Register register_4 (
    .D(ram_1_data), .Q(register_4_q), .clk(demultiplexer_1_out3), .clr(comparator_12_eq));  // open: en
  assign controlled_buffer_10_out = or_3_out ? adder_2_out : 8'bz;  // Controlled_Buffer controlled_buffer_13
  assign controlled_buffer_10_out = comparator_7_eq ? subtractor_1_out : 8'bz;  // Controlled_Buffer controlled_buffer_14
  nor nor_1 (nor_1_out, or_3_out, shift_register_1_q0, comparator_7_eq);
  assign controlled_buffer_15_out = comparator_9_eq ? adder_3_out : 8'bz;  // Controlled_Buffer controlled_buffer_15
  Adder adder_3 (.a(ram_1_data), .b(register_2_q), .out(adder_3_out));  // open: cin, cout
  assign controlled_buffer_15_out = comparator_10_eq ? subtractor_2_out : 8'bz;  // Controlled_Buffer controlled_buffer_16
  Subtractor subtractor_2 (.a(ram_1_data), .b(register_2_q), .out(subtractor_2_out));  // open: bin, bout
  Register register_5 (
    .D(ram_1_data), .Q({register_5_q_2, register_5_q}), .clk(demultiplexer_1_out1), .clr(comparator_12_eq));  // open: en
  assign controlled_buffer_10_out = nor_1_out ? register_6_q : 8'bz;  // Controlled_Buffer controlled_buffer_17
  assign controlled_buffer_15_out = nor_2_out ? ram_1_data : 8'bz;  // Controlled_Buffer controlled_buffer_18
  nor nor_2 (nor_2_out, comparator_9_eq, and_2_out, comparator_10_eq);
  Register register_6 (.D(controlled_buffer_10_out), .Q(register_6_q), .clk(button_1_out));  // open: en, clr
  RAM #(.bus("separate")) ram_1 (
    .addr(register_6_q), .din(controlled_buffer_15_out), .data(ram_1_data), .clk(button_1_out));  // open: str, sel, ld, clr
  Shifter shifter_1 (.in(register_3_q), .\dist (_011), .out(shifter_1_out));
  Comparator #(.width(3)) comparator_13 (.a(_011_2), .b(counter_2_q), .eq(comparator_13_eq));  // open: gt, lt
  // Probe on register_5_q
  // Probe on register_4_q
  // Probe on register_3_q
  // Probe on {register_5_q_2, register_5_q}
  // Probe on register_4_q
  // Probe on register_3_q
  assign controlled_buffer_19_out = d_ff_1_q ? comparator_13_eq : 1'bz;  // Controlled_Buffer controlled_buffer_19
  Adder adder_4 (.a(register_3_q), .b(register_4_q), .out(adder_4_out));  // open: cin, cout
  Subtractor subtractor_3 (.a(register_3_q), .b(register_4_q), .out(subtractor_3_out));  // open: bin, bout
  Multiplier multiplier_1 (.a(register_3_q), .b(register_4_q), .out(multiplier_1_out));  // open: cin, cout
  Divider divider_1 (.a(register_3_q), .b(register_4_q), .out(divider_1_out));  // open: upper, rem
  Shifter shifter_2 (.in(register_3_q), .\dist (_011_4), .out(shifter_2_out));
  assign controlled_buffer_15_out = and_2_out ? multiplexer_1_out : 8'bz;  // Controlled_Buffer controlled_buffer_20
  Comparator #(.width(3)) comparator_14 (.a(_011_5), .b(counter_2_q), .eq(comparator_14_eq));  // open: gt, lt
  Comparator comparator_15 (
    .a(register_3_q), .b(register_4_q), .gt(comparator_15_gt), .eq(comparator_15_eq), .lt(comparator_15_lt));
  // Probe on in_11
  // Probe on in_15
  // Probe on in_18
  Clock clock_1 (.out(clock_1_out));
  // Probe on divider_1_out
  // Probe on multiplier_1_out
  // Probe on subtractor_3_out
  // Probe on adder_4_out
  and and_1 (and_1_out, d_ff_3_q, comparator_14_eq);
  Comparator comparator_16 (.a(in_11), .b({register_5_q_2, register_5_q}), .eq(comparator_16_eq));  // open: gt, lt
  Comparator comparator_17 (.a(in_15), .b({register_5_q_2, register_5_q}), .eq(comparator_17_eq));  // open: gt, lt
  Comparator comparator_18 (.a(in_18), .b({register_5_q_2, register_5_q}), .eq(comparator_18_eq));  // open: gt, lt
  assign controlled_buffer_21_out = d_ff_1_q ? {shifter_1_out[7:4], register_4_q[3:0]} : 8'bz;  // Controlled_Buffer controlled_buffer_21
  Counter counter_3 (.Q(counter_3_q), .clk(clock_1_out));  // open: load, D, count, carry, clr
  not not_3 (not_3_out, d_ff_1_q);
  Comparator #(.width(3)) comparator_19 (.a(_011_3), .b(counter_2_q), .eq(comparator_19_eq));  // open: gt, lt
  and and_2 (and_2_out, d_ff_2_q, comparator_19_eq);
  and and_3 (and_3_out, comparator_15_gt, comparator_16_eq);
  assign controlled_buffer_21_out = not_3_out ? counter_3_q : 8'bz;  // Controlled_Buffer controlled_buffer_22
  Multiplexer #(.select(3), .width(8)) multiplexer_1 (
    .in0(adder_4_out), .in1(subtractor_3_out), .in2(multiplier_1_out), .in3(divider_1_out),
    .in4(shifter_2_out), .out(multiplexer_1_out), .sel(register_5_q));  // open: in5, in6, in7, en
  and and_4 (and_4_out, and_1_out, or_4_out);
  or or_4 (or_4_out, and_3_out, and_5_out, and_6_out);
  and and_5 (and_5_out, comparator_15_eq, comparator_17_eq);
  and and_6 (and_6_out, comparator_15_lt, comparator_18_eq);
  RAM #(.bus("separate")) ram_2 (
    .addr(controlled_buffer_21_out), .din({register_5_q_2, register_5_q}), .clk(controlled_buffer_19_out));  // open: data, str, sel, ld, clr

  // Notes on the sheet:
  //   такт
  //   забить бег по памяти
  //   вперед (пямять)
  //   назад (память)
  //   забить увеличения
  //   +
  //   -
  //   go to по пзу
  //   go to по озу
  //   if
  //   алу
  //   видеокарта
  //   contents of rom_1 (hex, n*v repeats v):
  //   4 1 1 1 5 2 5 5 2 5 5 3 3 9 2 2 7 5 2 5
  //   забить по битом по порядку 00000001 до 00001011
  //   11 команд начальную и 
  //   1100
  //   1101
  //   1110
  //   1111
  //   go to по озу
  //   go to по пзу
  //   движение по озу
  //   переменная
  //   00000001
  //   00000010
  //   00000011
  //   АЛУ
  //   IF
endmodule
